# Fritzing sketch stepper (saved by Fritzing 0.8.3b)
breadboards: 1

parts:
  Teensy1 = Teensy 2.0
  M1 = Stepper Motor - Bipolar
  MD09B1 = A4988 Stepper Motor Driver Carrier

nets:
  N1: Teensy1.GND, MD09B1.GROUND
  N2: Teensy1.D6, MD09B1.DIR
  N3: Teensy1.D7, MD09B1.STEP
  VCC: Teensy1.VCC, MD09B1.VDD
  N4: M1.A, MD09B1.OUT_2B
  N5: M1.C, MD09B1.OUT_2A
  N6: M1.B, MD09B1.OUT_1A
  N7: M1.D, MD09B1.OUT_1B
  N8: MD09B1.RESET, MD09B1.SLEEP

custom parts:
  Teensy 2.0: The Teensy is a complete USB-based microcontoller development system, in a very small footprint, capable of implementing many types of projects. All programming is done via the USB port. No special programmer is needed, only a standard "Mini-B" USB cable and a PC or Macintosh with a USB port.
